// Logisim project Simple_Computer_25Bit.circ as structural Verilog: 16 circuits, main circuit ADD_SUB
module Memory (
);

  wire Clock_Pulse_out, cpu_1_write_to_ram, Reset_out;
  wire [3:0] address_hex_1_n0, address_hex_1_n1, address_hex_1_n2, address_hex_1_n3, address_hex_1_n4,
       address_hex_2_n0, address_hex_2_n1, address_hex_2_n2, address_hex_2_n3, address_hex_2_n4,
       cpu_1_show_flags, Flags, flags_hex_1_cf, flags_hex_1_gf, flags_hex_1_lf, flags_hex_1_zf,
       number_hex_1_n0, number_hex_1_n1, number_hex_1_n2, number_hex_1_n3, number_hex_1_n4, number_hex_1_n6,
       number_hex_1_n7, number_hex_2_n0, number_hex_2_n1, number_hex_2_n2, number_hex_2_n3, number_hex_2_n4,
       number_hex_2_n6, number_hex_2_n7, number_hex_3_n0, number_hex_3_n1, number_hex_3_n2, number_hex_3_n3,
       number_hex_3_n4, number_hex_3_n6, number_hex_3_n7, Show_Flags_cf, Show_Flags_gf, Show_Flags_lf,
       Show_Flags_zf, Show_Value_n0, Show_Value_n1, Show_Value_n2, Show_Value_n3, Show_Value_n4,
       Show_Value_n6, Show_Value_n7;
  wire [19:0] cpu_1_address_to_ram, MAR, PC;
  wire [24:0] cpu_1_data_to_ram, cpu_1_show_number, MBR, RA, ram_1_dout, RX;

  Button Reset (.out(Reset_out));
  Clock Clock_Pulse (.out(Clock_Pulse_out));
  Hex_Digit_Display #(.decimalPoint("false")) hex_digit_display_1 (.value(number_hex_1_n7));
  Hex_Digit_Display #(.decimalPoint("false")) hex_digit_display_2 (.value(number_hex_1_n6));
  NUMBER_HEX number_hex_1 (
    .Number_25_Bits(RX), .N7(number_hex_1_n7), .N6(number_hex_1_n6), .N4(number_hex_1_n4),
    .N3(number_hex_1_n3), .N2(number_hex_1_n2), .N1(number_hex_1_n1), .N0(number_hex_1_n0));
  Hex_Digit_Display #(.decimalPoint("false")) hex_digit_display_3 (.value(number_hex_2_n7));
  Hex_Digit_Display #(.decimalPoint("false")) hex_digit_display_4 (.value(number_hex_2_n6));
  NUMBER_HEX number_hex_2 (
    .Number_25_Bits(MBR), .N7(number_hex_2_n7), .N6(number_hex_2_n6), .N4(number_hex_2_n4),
    .N3(number_hex_2_n3), .N2(number_hex_2_n2), .N1(number_hex_2_n1), .N0(number_hex_2_n0));
  Hex_Digit_Display #(.decimalPoint("false")) hex_digit_display_5 (.value(number_hex_1_n4));
  Hex_Digit_Display #(.decimalPoint("false")) hex_digit_display_6 (.value(number_hex_1_n3));
  // Probe on RX
  Hex_Digit_Display #(.decimalPoint("false")) hex_digit_display_7 (.value(number_hex_2_n4));
  Hex_Digit_Display #(.decimalPoint("false")) hex_digit_display_8 (.value(number_hex_2_n3));
  // Probe on MBR
  Hex_Digit_Display #(.decimalPoint("false")) hex_digit_display_9 (.value(Show_Flags_gf));
  Hex_Digit_Display #(.decimalPoint("false")) hex_digit_display_10 (.value(Show_Flags_lf));
  FLAGS_HEX Show_Flags (
    .Flags(cpu_1_show_flags), .GF(Show_Flags_gf), .LF(Show_Flags_lf), .ZF(Show_Flags_zf), .CF(Show_Flags_cf));
  // Probe on cpu_1_show_flags
  Hex_Digit_Display #(.decimalPoint("false")) hex_digit_display_11 (.value(number_hex_1_n2));
  Hex_Digit_Display #(.decimalPoint("false")) hex_digit_display_12 (.value(number_hex_1_n1));
  Hex_Digit_Display #(.decimalPoint("false")) hex_digit_display_13 (.value(number_hex_2_n2));
  Hex_Digit_Display #(.decimalPoint("false")) hex_digit_display_14 (.value(number_hex_2_n1));
  Hex_Digit_Display #(.decimalPoint("false")) hex_digit_display_15 (.value(Show_Flags_zf));
  Hex_Digit_Display #(.decimalPoint("false")) hex_digit_display_16 (.value(Show_Flags_cf));
  Hex_Digit_Display #(.decimalPoint("false")) hex_digit_display_17 (.value(number_hex_1_n0));
  Hex_Digit_Display #(.decimalPoint("false")) hex_digit_display_18 (.value(number_hex_2_n0));
  CPU cpu_1 (
    .Clock(Clock_Pulse_out), .Reset(Reset_out), .Data_from_RAM(ram_1_dout), .Show_Flags(cpu_1_show_flags),
    .Show_Number(cpu_1_show_number), .Address_to_RAM(cpu_1_address_to_ram),
    .Write_to_RAM(cpu_1_write_to_ram), .Data_to_RAM(cpu_1_data_to_ram), .PC_Value(PC), .MAR_Value(MAR),
    .MBR_Value(MBR), .RX_Value(RX), .RA_Value(RA), .Flags_Value(Flags));
  Hex_Digit_Display #(.decimalPoint("false")) hex_digit_display_19 (.value(number_hex_3_n7));
  Hex_Digit_Display #(.decimalPoint("false")) hex_digit_display_20 (.value(number_hex_3_n6));
  NUMBER_HEX number_hex_3 (
    .Number_25_Bits(RA), .N7(number_hex_3_n7), .N6(number_hex_3_n6), .N4(number_hex_3_n4),
    .N3(number_hex_3_n3), .N2(number_hex_3_n2), .N1(number_hex_3_n1), .N0(number_hex_3_n0));
  Hex_Digit_Display #(.decimalPoint("false")) hex_digit_display_21 (.value(address_hex_1_n4));
  Hex_Digit_Display #(.decimalPoint("false")) hex_digit_display_22 (.value(address_hex_1_n3));
  ADDRESS_HEX address_hex_1 (
    .Address_20_Bits(MAR), .N4(address_hex_1_n4), .N3(address_hex_1_n3), .N2(address_hex_1_n2),
    .N1(address_hex_1_n1), .N0(address_hex_1_n0));
  Hex_Digit_Display #(.decimalPoint("false")) hex_digit_display_23 (.value(Show_Value_n7));
  NUMBER_HEX Show_Value (
    .Number_25_Bits(cpu_1_show_number), .N7(Show_Value_n7), .N6(Show_Value_n6), .N4(Show_Value_n4),
    .N3(Show_Value_n3), .N2(Show_Value_n2), .N1(Show_Value_n1), .N0(Show_Value_n0));
  Hex_Digit_Display #(.decimalPoint("false")) hex_digit_display_24 (.value(number_hex_3_n4));
  Hex_Digit_Display #(.decimalPoint("false")) hex_digit_display_25 (.value(number_hex_3_n3));
  // Probe on RA
  Hex_Digit_Display #(.decimalPoint("false")) hex_digit_display_26 (.value(address_hex_1_n2));
  Hex_Digit_Display #(.decimalPoint("false")) hex_digit_display_27 (.value(address_hex_1_n1));
  // Probe on MAR
  Hex_Digit_Display #(.decimalPoint("false")) hex_digit_display_28 (.value(Show_Value_n6));
  Hex_Digit_Display #(.decimalPoint("false")) hex_digit_display_29 (.value(Show_Value_n4));
  RAM #(.addrWidth(20), .dataWidth(25), .enables("line")) ram_1 (
    .addr(cpu_1_address_to_ram), .we(cpu_1_write_to_ram), .clk(Clock_Pulse_out), .din(cpu_1_data_to_ram),
    .dout(ram_1_dout));
  Hex_Digit_Display #(.decimalPoint("false")) hex_digit_display_30 (.value(number_hex_3_n2));
  Hex_Digit_Display #(.decimalPoint("false")) hex_digit_display_31 (.value(number_hex_3_n1));
  Hex_Digit_Display #(.decimalPoint("false")) hex_digit_display_32 (.value(address_hex_1_n0));
  Hex_Digit_Display #(.decimalPoint("false")) hex_digit_display_33 (.value(Show_Value_n3));
  Hex_Digit_Display #(.decimalPoint("false")) hex_digit_display_34 (.value(Show_Value_n2));
  // Probe on cpu_1_show_number
  Hex_Digit_Display #(.decimalPoint("false")) hex_digit_display_35 (.value(number_hex_3_n0));
  Hex_Digit_Display #(.decimalPoint("false")) hex_digit_display_36 (.value(address_hex_2_n4));
  ADDRESS_HEX address_hex_2 (
    .Address_20_Bits(PC), .N4(address_hex_2_n4), .N3(address_hex_2_n3), .N2(address_hex_2_n2),
    .N1(address_hex_2_n1), .N0(address_hex_2_n0));
  Hex_Digit_Display #(.decimalPoint("false")) hex_digit_display_37 (.value(Show_Value_n1));
  Hex_Digit_Display #(.decimalPoint("false")) hex_digit_display_38 (.value(Show_Value_n0));
  Hex_Digit_Display #(.decimalPoint("false")) hex_digit_display_39 (.value(flags_hex_1_gf));
  Hex_Digit_Display #(.decimalPoint("false")) hex_digit_display_40 (.value(flags_hex_1_lf));
  FLAGS_HEX flags_hex_1 (
    .Flags(Flags), .GF(flags_hex_1_gf), .LF(flags_hex_1_lf), .ZF(flags_hex_1_zf), .CF(flags_hex_1_cf));
  // Probe on Flags
  Hex_Digit_Display #(.decimalPoint("false")) hex_digit_display_41 (.value(address_hex_2_n3));
  Hex_Digit_Display #(.decimalPoint("false")) hex_digit_display_42 (.value(address_hex_2_n2));
  // Probe on PC
  Hex_Digit_Display #(.decimalPoint("false")) hex_digit_display_43 (.value(flags_hex_1_zf));
  Hex_Digit_Display #(.decimalPoint("false")) hex_digit_display_44 (.value(flags_hex_1_cf));
  Hex_Digit_Display #(.decimalPoint("false")) hex_digit_display_45 (.value(address_hex_2_n1));
  Hex_Digit_Display #(.decimalPoint("false")) hex_digit_display_46 (.value(address_hex_2_n0));
endmodule

module CPU (
  input  Clock,
  input  Reset,
  input  [24:0] Data_from_RAM,
  output [3:0] Show_Flags,
  output [24:0] Show_Number,
  output [19:0] Address_to_RAM,
  output Write_to_RAM,
  output [24:0] Data_to_RAM,
  output [19:0] PC_Value,
  output [19:0] MAR_Value,
  output [24:0] MBR_Value,
  output [24:0] RX_Value,
  output [24:0] RA_Value,
  output [3:0] Flags_Value
);

  wire and_1_out, and_2_out, and_3_out, and_4_out, and_5_out, and_6_out, and_7_out, and_8_out, and_9_out,
       and_10_out, and_11_out, and_12_out, and_13_out, and_14_out, and_15_out, CF_New, CF_out, CF_WE,
       Clear_Flag_Number, cu_1_addmb, cu_1_andmb, cu_1_cmpmb, cu_1_divmb, cu_1_mulmb, cu_1_ngra, cu_1_ntra,
       cu_1_ormb, cu_1_shlra, cu_1_shrra, cu_1_submb, cu_1_xormb, decoder_1_out0, decoder_1_out1,
       decoder_1_out2, decoder_1_out3, GF_New, GF_out, GF_WE, LF_New, LF_out, LF_WE, MAR_from_MBR_Address,
       MAR_from_PC, MAR_WE, MBR_from_RA, MBR_from_RAM, MBR_from_RX, MBR_WE, not_1_out, not_2_out, or_1_out,
       or_7_out, PC_from_MBR_Address_if_GF, PC_from_MBR_Address_if_LF, PC_from_MBR_Address_if_ZF,
       PC_from_MBR_Address_unconditional, PC_inc, PC_WE, RA_from_MBR, RA_WE, register_1_q, register_2_q,
       RX_from_MBR, RX_WE, Set_Flag_Number, Show_Flags_t, Show_Memory_Value, Update_Flags, Update_RA,
       Update_RX, ZF_New, ZF_out, ZF_WE;
  wire [3:0] bit_extender_1_out;
  wire [19:0] MAR_New;
  wire [24:0] bit_extender_2_out, MBR_New, multiplexer_4_out, RA_New, RA_out, register_3_q, RX_New, RX_out;

  Counter #(.max('hfffff), .width(20)) PC (
    .load(PC_WE), .D(Data_to_RAM[19:0]), .count(PC_inc), .Q(PC_Value), .clk(Clock), .clr(Reset));  // open: carry, up
  or or_1 (or_1_out, Set_Flag_Number, Clear_Flag_Number);
  Decoder #(.enable("false"), .select(2)) decoder_1 (
    .out0(decoder_1_out0), .out1(decoder_1_out1), .out2(decoder_1_out2), .out3(decoder_1_out3),
    .sel(Data_to_RAM[1:0]));
  CU cu_1 (
    .IR(Data_to_RAM[24:20]), .Clock(Clock), .Reset(Reset), .pcinc(PC_inc),
    .pcmb(PC_from_MBR_Address_unconditional), .pcmbz(PC_from_MBR_Address_if_ZF),
    .pcmbl(PC_from_MBR_Address_if_LF), .pcmbg(PC_from_MBR_Address_if_GF), .mapc(MAR_from_PC),
    .mamb(MAR_from_MBR_Address), .mbm(MBR_from_RAM), .mbra(MBR_from_RA), .mbrx(MBR_from_RX),
    .rxmb(RX_from_MBR), .mmb(Write_to_RAM), .ramb(RA_from_MBR), .ntra(cu_1_ntra), .ngra(cu_1_ngra),
    .andmb(cu_1_andmb), .ormb(cu_1_ormb), .xormb(cu_1_xormb), .addmb(cu_1_addmb), .submb(cu_1_submb),
    .mulmb(cu_1_mulmb), .divmb(cu_1_divmb), .shlra(cu_1_shlra), .shrra(cu_1_shrra), .cmpmb(cu_1_cmpmb),
    .setflgn(Set_Flag_Number), .clrflgn(Clear_Flag_Number), .showflgs(Show_Flags_t),
    .showmval(Show_Memory_Value), .urx(Update_RX), .ura(Update_RA), .uf(Update_Flags));
  and and_1 (and_1_out, or_1_out, decoder_1_out0);
  and and_2 (and_2_out, or_1_out, decoder_1_out1);
  and and_3 (and_3_out, or_1_out, decoder_1_out2);
  and and_4 (and_4_out, or_1_out, decoder_1_out3);
  and and_5 (and_5_out, PC_from_MBR_Address_if_ZF, Flags_Value[1]);
  and and_6 (and_6_out, PC_from_MBR_Address_if_LF, Flags_Value[2]);
  and and_7 (and_7_out, PC_from_MBR_Address_if_GF, Flags_Value[3]);
  or or_2 (CF_WE, and_1_out, Update_Flags);
  or or_3 (ZF_WE, and_2_out, Update_Flags);
  or or_4 (LF_WE, and_3_out, Update_Flags);
  or or_5 (GF_WE, and_4_out, Update_Flags);
  or or_6 (PC_WE, and_5_out, and_6_out, and_7_out, PC_from_MBR_Address_unconditional);
  not not_1 (not_1_out, Clear_Flag_Number);
  or or_7 (or_7_out, Set_Flag_Number, Clear_Flag_Number);
  not not_2 (not_2_out, or_7_out);
  and and_8 (and_8_out, Set_Flag_Number, not_1_out);
  and and_9 (and_9_out, Set_Flag_Number, not_1_out);
  and and_10 (and_10_out, Set_Flag_Number, not_1_out);
  and and_11 (and_11_out, Set_Flag_Number, not_1_out);
  Register #(.width(1)) GF (.D(GF_New), .en(GF_WE), .clk(Clock), .Q(Flags_Value[3]), .clr(Reset));
  or or_8 (MAR_WE, MAR_from_PC, MAR_from_MBR_Address);
  or or_9 (MBR_WE, MBR_from_RAM, MBR_from_RA, MBR_from_RX);
  ALU alu_1 (
    .ntra(cu_1_ntra), .ngra(cu_1_ngra), .andmb(cu_1_andmb), .ormb(cu_1_ormb), .xormb(cu_1_xormb),
    .addmb(cu_1_addmb), .submb(cu_1_submb), .mulmb(cu_1_mulmb), .divmb(cu_1_divmb), .shlra(cu_1_shlra),
    .shrra(cu_1_shrra), .cmpmb(cu_1_cmpmb), .RA_Old(RA_Value), .MBR(Data_to_RAM), .CF_Old(Flags_Value[0]),
    .ZF_Old(Flags_Value[1]), .LF_Old(Flags_Value[2]), .GF_Old(Flags_Value[3]), .RX_New(RX_out),
    .RA_New(RA_out), .CF_New(CF_out), .ZF_New(ZF_out), .LF_New(LF_out), .GF_New(GF_out));
  and and_12 (and_12_out, not_2_out, CF_out);
  and and_13 (and_13_out, not_2_out, ZF_out);
  and and_14 (and_14_out, not_2_out, LF_out);
  and and_15 (and_15_out, not_2_out, GF_out);
  or or_10 (CF_New, and_12_out, and_8_out);
  or or_11 (ZF_New, and_13_out, and_9_out);
  or or_12 (LF_New, and_14_out, and_10_out);
  or or_13 (GF_New, and_15_out, and_11_out);
  or or_14 (RX_WE, RX_from_MBR, Update_RX);
  or or_15 (RA_WE, RA_from_MBR, Update_RA);
  Register #(.width(1)) LF (.D(LF_New), .en(LF_WE), .clk(Clock), .Q(Flags_Value[2]), .clr(Reset));
  Register #(.width(20)) MAR (.D(MAR_New), .en(MAR_WE), .clk(Clock), .Q(Address_to_RAM), .clr(Reset));
  Register #(.width(1)) ZF (.D(ZF_New), .en(ZF_WE), .clk(Clock), .Q(Flags_Value[1]), .clr(Reset));
  Multiplexer #(.width(25)) multiplexer_1 (.in0(RX_out), .in1(Data_to_RAM), .out(RX_New), .sel(RX_from_MBR));
  Multiplexer #(.width(25)) multiplexer_2 (.in0(RA_out), .in1(Data_to_RAM), .out(RA_New), .sel(RA_from_MBR));
  Multiplexer #(.width(20)) multiplexer_3 (
    .in0(PC_Value), .in1(Data_to_RAM[19:0]), .out(MAR_New), .sel(MAR_from_MBR_Address));
  Multiplexer #(.width(25)) multiplexer_4 (.in0(RA_Value), .in1(RX_Value), .out(multiplexer_4_out), .sel(MBR_from_RX));
  Register #(.width(25)) RX (.D(RX_New), .en(RX_WE), .clk(Clock), .Q(RX_Value), .clr(Reset));
  Multiplexer #(.width(25)) multiplexer_5 (
    .in0(multiplexer_4_out), .in1(Data_from_RAM), .out(MBR_New), .sel(MBR_from_RAM));
  Register #(.width(25)) MBR (.D(MBR_New), .en(MBR_WE), .clk(Clock), .Q(Data_to_RAM), .clr(Reset));
  Register #(.width(1)) CF (.D(CF_New), .en(CF_WE), .clk(Clock), .Q(Flags_Value[0]), .clr(Reset));
  Register #(.width(25)) RA (.D(RA_New), .en(RA_WE), .clk(Clock), .Q(RA_Value), .clr(Reset));
  Register #(.width(1)) register_1 (.D(Show_Flags_t), .en(Show_Flags_t), .clk(Clock), .Q(register_1_q), .clr(Reset));
  Register #(.width(1)) register_2 (
    .D(Show_Memory_Value), .en(Show_Memory_Value), .clk(Clock), .Q(register_2_q), .clr(Reset));
  assign bit_extender_1_out = {{3{register_1_q}}, register_1_q};  // Bit_Extender bit_extender_1
  assign Show_Flags = Flags_Value & bit_extender_1_out;  // AND_Gate and_16, 4 bits wide
  assign bit_extender_2_out = {{24{register_2_q}}, register_2_q};  // Bit_Extender bit_extender_2
  Register #(.width(25)) register_3 (
    .D(Data_to_RAM), .en(Show_Memory_Value), .clk(Clock), .Q(register_3_q), .clr(Reset));
  assign Show_Number = bit_extender_2_out & register_3_q;  // AND_Gate and_17, 25 bits wide

  assign MAR_Value = Address_to_RAM;
  assign MBR_Value = Data_to_RAM;

  // Other names for the same wires on the sheet: CF = Flags_Value[0]; ZF = Flags_Value[1]; LF = Flags_Value[2];
  //   GF = Flags_Value[3]; MAR[19:0] = Address_to_RAM; Flag_Number[1:0] = Data_to_RAM[1:0]; MBR[24:0] = Data_to_RAM;
  //   MBR_Address[19:0] = Data_to_RAM[19:0]; MBR_OpCode[4:0] = Data_to_RAM[24:20]; PC[19:0] = PC_Value;
  //   RA[24:0] = RA_Value; RAM_from_MBR = Write_to_RAM; RX[24:0] = RX_Value
endmodule

module ALU (
  input  ntra,
  input  ngra,
  input  andmb,
  input  ormb,
  input  xormb,
  input  addmb,
  input  submb,
  input  mulmb,
  input  divmb,
  input  shlra,
  input  shrra,
  input  cmpmb,
  input  [24:0] RA_Old,
  input  [24:0] MBR,
  input  CF_Old,
  input  ZF_Old,
  input  LF_Old,
  input  GF_Old,
  output [24:0] RX_New,
  output [24:0] RA_New,
  output CF_New,
  output ZF_New,
  output LF_New,
  output GF_New
);

  wire add_sub_1_carry, add_sub_2_carry, and_2_out, and_3_out, and_4_out, and_5_out, comparator_1_eq,
       comparator_1_gt, comparator_1_lt, or_2_out, or_3_out, shift_left_1_carry_new, shift_right_1_carry_new;
  wire [24:0] add_sub_1_result, add_sub_2_result, and_1_out, and_6_out, and_7_out, and_8_out, and_9_out,
       and_10_out, and_11_out, and_12_out, and_13_out, and_14_out, and_15_out, and_16_out, and_17_out,
       and_18_out, bit_extender_1_out, bit_extender_2_out, bit_extender_3_out, bit_extender_4_out,
       bit_extender_5_out, bit_extender_6_out, bit_extender_7_out, bit_extender_8_out, bit_extender_9_out,
       bit_extender_10_out, bit_extender_11_out, divide_1_remainder, divide_1_result,
       multiply_1_result_higherhalf, multiply_1_result_lowerhalf, negator_1_out, not_1_out, or_1_out,
       shift_left_1_result, shift_right_1_result, xor_1_out;

  assign not_1_out = ~RA_Old;  // NOT_Gate not_1, 25 bits wide
  assign and_1_out = RA_Old & MBR;  // AND_Gate and_1, 25 bits wide
  assign or_1_out = RA_Old | MBR;  // OR_Gate or_1, 25 bits wide
  Negator #(.width(25)) negator_1 (.in(RA_Old), .out(negator_1_out));
  assign xor_1_out = RA_Old ^ MBR;  // XOR_Gate xor_1, 25 bits wide
  ADD_SUB add_sub_1 (.Mode(1'b0), .A(RA_Old), .B(MBR), .Result(add_sub_1_result), .Carry(add_sub_1_carry));
  ADD_SUB add_sub_2 (.Mode(1'b1), .A(RA_Old), .B(MBR), .Result(add_sub_2_result), .Carry(add_sub_2_carry));
  MULTIPLY multiply_1 (
    .A(RA_Old), .B(MBR), .Result_HigherHalf(multiply_1_result_higherhalf),
    .Result_LowerHalf(multiply_1_result_lowerhalf));
  DIVIDE divide_1 (.A(RA_Old), .B(MBR), .Result(divide_1_result), .Remainder(divide_1_remainder));
  SHIFT_LEFT shift_left_1 (
    .Carry_Old(CF_Old), .Number(RA_Old), .Result(shift_left_1_result), .Carry_New(shift_left_1_carry_new));
  SHIFT_RIGHT shift_right_1 (
    .Carry_Old(CF_Old), .Number(RA_Old), .Result(shift_right_1_result), .Carry_New(shift_right_1_carry_new));
  Comparator #(.width(25)) comparator_1 (
    .a(RA_Old), .b(MBR), .gt(comparator_1_gt), .eq(comparator_1_eq), .lt(comparator_1_lt));
  assign bit_extender_1_out = {{24{ntra}}, ntra};  // Bit_Extender bit_extender_1
  assign bit_extender_2_out = {{24{ngra}}, ngra};  // Bit_Extender bit_extender_2
  and and_2 (and_2_out, add_sub_1_carry, addmb);
  and and_3 (and_3_out, add_sub_2_carry, submb);
  or or_2 (or_2_out, and_2_out, and_3_out, and_4_out, and_5_out);
  assign bit_extender_3_out = {{24{andmb}}, andmb};  // Bit_Extender bit_extender_3
  and and_4 (and_4_out, shift_left_1_carry_new, shlra);
  and and_5 (and_5_out, shift_right_1_carry_new, shrra);
  assign bit_extender_4_out = {{24{ormb}}, ormb};  // Bit_Extender bit_extender_4
  assign bit_extender_5_out = {{24{xormb}}, xormb};  // Bit_Extender bit_extender_5
  or or_3 (or_3_out, addmb, submb, shlra, shrra);
  assign bit_extender_6_out = {{24{addmb}}, addmb};  // Bit_Extender bit_extender_6
  assign bit_extender_7_out = {{24{submb}}, submb};  // Bit_Extender bit_extender_7
  assign bit_extender_8_out = {{24{mulmb}}, mulmb};  // Bit_Extender bit_extender_8
  assign bit_extender_9_out = {{24{divmb}}, divmb};  // Bit_Extender bit_extender_9
  assign bit_extender_10_out = {{24{shlra}}, shlra};  // Bit_Extender bit_extender_10
  assign bit_extender_11_out = {{24{shrra}}, shrra};  // Bit_Extender bit_extender_11
  assign and_6_out = bit_extender_8_out & multiply_1_result_higherhalf;  // AND_Gate and_6, 25 bits wide
  assign and_7_out = bit_extender_9_out & divide_1_remainder;  // AND_Gate and_7, 25 bits wide
  assign and_8_out = bit_extender_1_out & not_1_out;  // AND_Gate and_8, 25 bits wide
  assign and_9_out = bit_extender_2_out & negator_1_out;  // AND_Gate and_9, 25 bits wide
  assign and_10_out = bit_extender_3_out & and_1_out;  // AND_Gate and_10, 25 bits wide
  assign and_11_out = bit_extender_4_out & or_1_out;  // AND_Gate and_11, 25 bits wide
  assign and_12_out = bit_extender_5_out & xor_1_out;  // AND_Gate and_12, 25 bits wide
  assign and_13_out = bit_extender_6_out & add_sub_1_result;  // AND_Gate and_13, 25 bits wide
  assign and_14_out = bit_extender_7_out & add_sub_2_result;  // AND_Gate and_14, 25 bits wide
  assign and_15_out = bit_extender_8_out & multiply_1_result_lowerhalf;  // AND_Gate and_15, 25 bits wide
  assign and_16_out = bit_extender_9_out & divide_1_result;  // AND_Gate and_16, 25 bits wide
  assign and_17_out = bit_extender_10_out & shift_left_1_result;  // AND_Gate and_17, 25 bits wide
  assign and_18_out = bit_extender_11_out & shift_right_1_result;  // AND_Gate and_18, 25 bits wide
  UPDATE_FLAG update_flag_1 (.Change(cmpmb), .Old_Flag(ZF_Old), .New_Flag(comparator_1_eq), .Updated_Flag(ZF_New));
  UPDATE_FLAG update_flag_2 (.Change(cmpmb), .Old_Flag(LF_Old), .New_Flag(comparator_1_lt), .Updated_Flag(LF_New));
  UPDATE_FLAG update_flag_3 (.Change(cmpmb), .Old_Flag(GF_Old), .New_Flag(comparator_1_gt), .Updated_Flag(GF_New));
  UPDATE_FLAG update_flag_4 (.Change(or_3_out), .Old_Flag(CF_Old), .New_Flag(or_2_out), .Updated_Flag(CF_New));
  assign RX_New = and_6_out | and_7_out;  // OR_Gate or_4, 25 bits wide
  assign RA_New = and_8_out | and_9_out | and_10_out | and_11_out | and_12_out | and_13_out | and_14_out | and_15_out | and_16_out | and_17_out | and_18_out;  // OR_Gate or_5, 25 bits wide
endmodule

module CU (
  input  [4:0] IR,
  input  Clock,
  input  Reset,
  output pcinc,
  output pcmb,
  output pcmbz,
  output pcmbl,
  output pcmbg,
  output mapc,
  output mamb,
  output mbm,
  output mbra,
  output mbrx,
  output rxmb,
  output mmb,
  output ramb,
  output ntra,
  output ngra,
  output andmb,
  output ormb,
  output xormb,
  output addmb,
  output submb,
  output mulmb,
  output divmb,
  output shlra,
  output shrra,
  output cmpmb,
  output setflgn,
  output clrflgn,
  output showflgs,
  output showmval,
  output urx,
  output ura,
  output uf
);

  wire and_1_out, decoder_1_out30, not_1_out, or_1_out;
  wire [6:0] counter_1_q;
  wire [7:0] rom_1_data;

  Counter #(.max('h7f), .width(7)) counter_1 (
    .load(rom_1_data[2]), .D({IR, 2'b11}), .count(rom_1_data[0]), .Q(counter_1_q), .clk(and_1_out),
    .clr(or_1_out));  // open: carry, up
  and and_1 (and_1_out, Clock, not_1_out);
  ROM #(.addrWidth(7)) rom_1 (.addr(counter_1_q), .data(rom_1_data));
  or or_1 (or_1_out, rom_1_data[1], Reset);
  not not_1 (not_1_out, decoder_1_out30);
  Decoder #(.enable("false"), .select(5)) decoder_1 (
    .out1(pcinc), .out2(pcmb), .out3(pcmbz), .out4(pcmbl), .out5(pcmbg), .out6(mapc), .out7(mamb),
    .out8(mbm), .out9(mbra), .out10(mbrx), .out11(rxmb), .out12(mmb), .out13(ramb), .out14(ntra),
    .out15(ngra), .out16(andmb), .out17(ormb), .out18(xormb), .out19(addmb), .out20(submb), .out21(mulmb),
    .out22(divmb), .out23(shlra), .out24(shrra), .out25(cmpmb), .out26(setflgn), .out27(clrflgn),
    .out28(showflgs), .out29(showmval), .out30(decoder_1_out30), .sel(rom_1_data[7:3]));  // open: out0, out31
  or or_2 (urx, mulmb, divmb);
  or or_3 (ura, ntra, ngra, andmb, ormb, xormb, addmb, submb, mulmb, divmb, shlra, shrra);
  or or_4 (uf, addmb, submb, shlra, shrra, cmpmb);

  // Notes on the sheet:
  //   contents of rom_1 (hex, n*v repeats v):
  //   31 41 c 4*2 d1 2 2 2 d9 2 2 2 71 2 2 2 79 2 2 2 39 41 81 2 39 41 89 2 39 41 91 2 39 41 99 2 39 41 a1
  //   2 39 41 a9 2 39 41 b1 2 b9 2 2 2 c1 2 2 2 39 41 c9 2 11 2 2 2 19 2 2 2 21 2 2 2 29 2 2 2 39 41 69 2
  //   39 41 59 2 39 49 61 2 39 51 61 2 e1 2 2 2 39 41 e9 2 f2
endmodule

module NUMBER_HEX (
  input  [24:0] Number_25_Bits,
  output [3:0] N7,
  output [3:0] N6,
  output [3:0] N4,
  output [3:0] N3,
  output [3:0] N2,
  output [3:0] N1,
  output [3:0] N0
);

  assign {N7, N6, N4, N3, N2, N1, N0} = {{3{1'b0}}, Number_25_Bits};  // Bit_Extender bit_extender_1
endmodule

module ADDRESS_HEX (
  input  [19:0] Address_20_Bits,
  output [3:0] N4,
  output [3:0] N3,
  output [3:0] N2,
  output [3:0] N1,
  output [3:0] N0
);


  assign N0 = Address_20_Bits[3:0];
  assign N1 = Address_20_Bits[7:4];
  assign N2 = Address_20_Bits[11:8];
  assign N3 = Address_20_Bits[15:12];
  assign N4 = Address_20_Bits[19:16];
endmodule

module FLAGS_HEX (
  input  [3:0] Flags,
  output [3:0] GF,
  output [3:0] LF,
  output [3:0] ZF,
  output [3:0] CF
);

  assign CF = {{3{1'b0}}, Flags[0]};  // Bit_Extender bit_extender_1
  assign ZF = {{3{1'b0}}, Flags[1]};  // Bit_Extender bit_extender_2
  assign LF = {{3{1'b0}}, Flags[2]};  // Bit_Extender bit_extender_3
  assign GF = {{3{1'b0}}, Flags[3]};  // Bit_Extender bit_extender_4
endmodule

module UPDATE_FLAG (
  input  Change,
  input  Old_Flag,
  input  New_Flag,
  output Updated_Flag
);

  wire and_1_out, and_2_out, not_1_out;

  not not_1 (not_1_out, Change);
  and and_1 (and_1_out, not_1_out, Old_Flag);
  and and_2 (and_2_out, Change, New_Flag);
  or or_1 (Updated_Flag, and_1_out, and_2_out);
endmodule

module ADD_SUB (
  input  Mode,
  input  [24:0] A,
  input  [24:0] B,
  output [24:0] Result,
  output Carry
);

  wire add_sub_1bit_1_carry_out, add_sub_1bit_2_carry_out, add_sub_1bit_3_carry_out,
       add_sub_1bit_4_carry_out, add_sub_1bit_5_carry_out, add_sub_1bit_6_carry_out,
       add_sub_1bit_7_carry_out, add_sub_1bit_8_carry_out, add_sub_1bit_9_carry_out,
       add_sub_1bit_10_carry_out, add_sub_1bit_11_carry_out, add_sub_1bit_12_carry_out,
       add_sub_1bit_13_carry_out, add_sub_1bit_14_carry_out, add_sub_1bit_15_carry_out,
       add_sub_1bit_16_carry_out, add_sub_1bit_17_carry_out, add_sub_1bit_18_carry_out,
       add_sub_1bit_19_carry_out, add_sub_1bit_20_carry_out, add_sub_1bit_21_carry_out,
       add_sub_1bit_22_carry_out, add_sub_1bit_23_carry_out, add_sub_1bit_24_carry_out;
  wire [24:0] bit_extender_1_out, xor_1_out;

  assign bit_extender_1_out = {{24{Mode}}, Mode};  // Bit_Extender bit_extender_1
  assign xor_1_out = bit_extender_1_out ^ B;  // XOR_Gate xor_1, 25 bits wide
  ADD_SUB_1BIT add_sub_1bit_1 (
    .Carry_In(Mode), .A(A[0]), .B(xor_1_out[0]), .Sum(Result[0]), .Carry_Out(add_sub_1bit_1_carry_out));
  ADD_SUB_1BIT add_sub_1bit_2 (
    .Carry_In(add_sub_1bit_1_carry_out), .A(A[1]), .B(xor_1_out[1]), .Sum(Result[1]),
    .Carry_Out(add_sub_1bit_2_carry_out));
  ADD_SUB_1BIT add_sub_1bit_3 (
    .Carry_In(add_sub_1bit_2_carry_out), .A(A[2]), .B(xor_1_out[2]), .Sum(Result[2]),
    .Carry_Out(add_sub_1bit_3_carry_out));
  ADD_SUB_1BIT add_sub_1bit_4 (
    .Carry_In(add_sub_1bit_3_carry_out), .A(A[3]), .B(xor_1_out[3]), .Sum(Result[3]),
    .Carry_Out(add_sub_1bit_4_carry_out));
  ADD_SUB_1BIT add_sub_1bit_5 (
    .Carry_In(add_sub_1bit_4_carry_out), .A(A[4]), .B(xor_1_out[4]), .Sum(Result[4]),
    .Carry_Out(add_sub_1bit_5_carry_out));
  ADD_SUB_1BIT add_sub_1bit_6 (
    .Carry_In(add_sub_1bit_5_carry_out), .A(A[5]), .B(xor_1_out[5]), .Sum(Result[5]),
    .Carry_Out(add_sub_1bit_6_carry_out));
  ADD_SUB_1BIT add_sub_1bit_7 (
    .Carry_In(add_sub_1bit_6_carry_out), .A(A[6]), .B(xor_1_out[6]), .Sum(Result[6]),
    .Carry_Out(add_sub_1bit_7_carry_out));
  ADD_SUB_1BIT add_sub_1bit_8 (
    .Carry_In(add_sub_1bit_7_carry_out), .A(A[7]), .B(xor_1_out[7]), .Sum(Result[7]),
    .Carry_Out(add_sub_1bit_8_carry_out));
  ADD_SUB_1BIT add_sub_1bit_9 (
    .Carry_In(add_sub_1bit_8_carry_out), .A(A[8]), .B(xor_1_out[8]), .Sum(Result[8]),
    .Carry_Out(add_sub_1bit_9_carry_out));
  ADD_SUB_1BIT add_sub_1bit_10 (
    .Carry_In(add_sub_1bit_9_carry_out), .A(A[9]), .B(xor_1_out[9]), .Sum(Result[9]),
    .Carry_Out(add_sub_1bit_10_carry_out));
  ADD_SUB_1BIT add_sub_1bit_11 (
    .Carry_In(add_sub_1bit_10_carry_out), .A(A[10]), .B(xor_1_out[10]), .Sum(Result[10]),
    .Carry_Out(add_sub_1bit_11_carry_out));
  ADD_SUB_1BIT add_sub_1bit_12 (
    .Carry_In(add_sub_1bit_11_carry_out), .A(A[11]), .B(xor_1_out[11]), .Sum(Result[11]),
    .Carry_Out(add_sub_1bit_12_carry_out));
  ADD_SUB_1BIT add_sub_1bit_13 (
    .Carry_In(add_sub_1bit_12_carry_out), .A(A[12]), .B(xor_1_out[12]), .Sum(Result[12]),
    .Carry_Out(add_sub_1bit_13_carry_out));
  ADD_SUB_1BIT add_sub_1bit_14 (
    .Carry_In(add_sub_1bit_13_carry_out), .A(A[13]), .B(xor_1_out[13]), .Sum(Result[13]),
    .Carry_Out(add_sub_1bit_14_carry_out));
  ADD_SUB_1BIT add_sub_1bit_15 (
    .Carry_In(add_sub_1bit_14_carry_out), .A(A[14]), .B(xor_1_out[14]), .Sum(Result[14]),
    .Carry_Out(add_sub_1bit_15_carry_out));
  ADD_SUB_1BIT add_sub_1bit_16 (
    .Carry_In(add_sub_1bit_15_carry_out), .A(A[15]), .B(xor_1_out[15]), .Sum(Result[15]),
    .Carry_Out(add_sub_1bit_16_carry_out));
  ADD_SUB_1BIT add_sub_1bit_17 (
    .Carry_In(add_sub_1bit_16_carry_out), .A(A[16]), .B(xor_1_out[16]), .Sum(Result[16]),
    .Carry_Out(add_sub_1bit_17_carry_out));
  ADD_SUB_1BIT add_sub_1bit_18 (
    .Carry_In(add_sub_1bit_17_carry_out), .A(A[17]), .B(xor_1_out[17]), .Sum(Result[17]),
    .Carry_Out(add_sub_1bit_18_carry_out));
  ADD_SUB_1BIT add_sub_1bit_19 (
    .Carry_In(add_sub_1bit_18_carry_out), .A(A[18]), .B(xor_1_out[18]), .Sum(Result[18]),
    .Carry_Out(add_sub_1bit_19_carry_out));
  ADD_SUB_1BIT add_sub_1bit_20 (
    .Carry_In(add_sub_1bit_19_carry_out), .A(A[19]), .B(xor_1_out[19]), .Sum(Result[19]),
    .Carry_Out(add_sub_1bit_20_carry_out));
  ADD_SUB_1BIT add_sub_1bit_21 (
    .Carry_In(add_sub_1bit_20_carry_out), .A(A[20]), .B(xor_1_out[20]), .Sum(Result[20]),
    .Carry_Out(add_sub_1bit_21_carry_out));
  ADD_SUB_1BIT add_sub_1bit_22 (
    .Carry_In(add_sub_1bit_21_carry_out), .A(A[21]), .B(xor_1_out[21]), .Sum(Result[21]),
    .Carry_Out(add_sub_1bit_22_carry_out));
  ADD_SUB_1BIT add_sub_1bit_23 (
    .Carry_In(add_sub_1bit_22_carry_out), .A(A[22]), .B(xor_1_out[22]), .Sum(Result[22]),
    .Carry_Out(add_sub_1bit_23_carry_out));
  ADD_SUB_1BIT add_sub_1bit_24 (
    .Carry_In(add_sub_1bit_23_carry_out), .A(A[23]), .B(xor_1_out[23]), .Sum(Result[23]),
    .Carry_Out(add_sub_1bit_24_carry_out));
  ADD_SUB_1BIT add_sub_1bit_25 (
    .Carry_In(add_sub_1bit_24_carry_out), .A(A[24]), .B(xor_1_out[24]), .Sum(Result[24]), .Carry_Out(Carry));
endmodule

module ADD_SUB_1BIT (
  input  Carry_In,
  input  A,
  input  B,
  output Sum,
  output Carry_Out
);

  wire and_1_out, and_2_out, xor_1_out;

  xor xor_1 (xor_1_out, A, B);
  and and_1 (and_1_out, A, B);
  or or_1 (Carry_Out, and_1_out, and_2_out);
  xor xor_2 (Sum, Carry_In, xor_1_out);
  and and_2 (and_2_out, Carry_In, xor_1_out);
endmodule

module MULTIPLY (
  input  [24:0] A,
  input  [24:0] B,
  output [24:0] Result_HigherHalf,
  output [24:0] Result_LowerHalf
);

  wire add_sub_1_carry, make_positive_1_previous_sign, make_positive_2_previous_sign, xor_1_out;
  wire [24:0] bit_extender_1_out, bit_extender_2_out, make_positive_1_result, make_positive_2_result,
       multiplexer_1_out, multiplexer_2_out, multiplier_1_cout, multiplier_1_out, not_1_out, not_2_out;

  MAKE_POSITIVE make_positive_1 (
    .Number(A), .Result(make_positive_1_result), .Previous_Sign(make_positive_1_previous_sign));
  MAKE_POSITIVE make_positive_2 (
    .Number(B), .Result(make_positive_2_result), .Previous_Sign(make_positive_2_previous_sign));
  xor xor_1 (xor_1_out, make_positive_1_previous_sign, make_positive_2_previous_sign);
  Multiplier #(.width(25)) multiplier_1 (
    .a(make_positive_1_result), .b(make_positive_2_result), .out(multiplier_1_out), .cin({25{1'b0}}),
    .cout(multiplier_1_cout));
  assign not_1_out = ~multiplier_1_out;  // NOT_Gate not_1, 25 bits wide
  assign not_2_out = ~multiplier_1_cout;  // NOT_Gate not_2, 25 bits wide
  Multiplexer #(.width(25)) multiplexer_1 (
    .in0(multiplier_1_out), .in1(not_1_out), .out(multiplexer_1_out), .sel(xor_1_out));
  Multiplexer #(.width(25)) multiplexer_2 (
    .in0(multiplier_1_cout), .in1(not_2_out), .out(multiplexer_2_out), .sel(xor_1_out));
  assign bit_extender_1_out = {{24{1'b0}}, xor_1_out};  // Bit_Extender bit_extender_1
  ADD_SUB add_sub_1 (
    .Mode(1'b0), .A(bit_extender_1_out), .B(multiplexer_1_out), .Result(Result_LowerHalf),
    .Carry(add_sub_1_carry));
  assign bit_extender_2_out = {{24{1'b0}}, add_sub_1_carry};  // Bit_Extender bit_extender_2
  ADD_SUB add_sub_2 (
    .Mode(1'b0), .A(bit_extender_2_out), .B(multiplexer_2_out), .Result(Result_HigherHalf));  // open: Carry
endmodule

module DIVIDE (
  input  [24:0] A,
  input  [24:0] B,
  output [24:0] Result,
  output [24:0] Remainder
);

  wire make_positive_1_previous_sign, make_positive_2_previous_sign, xor_1_out;
  wire [24:0] divider_1_out, divider_1_rem, make_positive_1_result, make_positive_2_result, negator_1_out,
       negator_2_out;

  MAKE_POSITIVE make_positive_1 (
    .Number(A), .Result(make_positive_1_result), .Previous_Sign(make_positive_1_previous_sign));
  MAKE_POSITIVE make_positive_2 (
    .Number(B), .Result(make_positive_2_result), .Previous_Sign(make_positive_2_previous_sign));
  xor xor_1 (xor_1_out, make_positive_1_previous_sign, make_positive_2_previous_sign);
  Divider #(.width(25)) divider_1 (
    .a(make_positive_1_result), .b(make_positive_2_result), .out(divider_1_out), .upper({25{1'b0}}),
    .rem(divider_1_rem));
  Negator #(.width(25)) negator_1 (.in(divider_1_rem), .out(negator_1_out));
  Negator #(.width(25)) negator_2 (.in(divider_1_out), .out(negator_2_out));
  Multiplexer #(.width(25)) multiplexer_1 (.in0(divider_1_out), .in1(negator_2_out), .out(Result), .sel(xor_1_out));
  Multiplexer #(.width(25)) multiplexer_2 (
    .in0(divider_1_rem), .in1(negator_1_out), .out(Remainder), .sel(make_positive_1_previous_sign));
endmodule

module SHIFT_LEFT (
  input  [24:0] Number,
  input  Carry_Old,
  output [24:0] Result,
  output Carry_New
);


  assign Carry_New = Number[24];
  assign Result = {Number[23:0], Carry_Old};
endmodule

module SHIFT_RIGHT (
  input  [24:0] Number,
  input  Carry_Old,
  output [24:0] Result,
  output Carry_New
);


  assign Carry_New = Number[0];
  assign Result = {Carry_Old, Number[24:1]};
endmodule

module MAKE_POSITIVE (
  input  [24:0] Number,
  output [24:0] Result,
  output Previous_Sign
);

  wire [24:0] negator_1_out;

  Negator #(.width(25)) negator_1 (.in(Number), .out(negator_1_out));
  SIGN_BIT sign_bit_1 (.Number(Number), .Is_Negative(Previous_Sign));
  Multiplexer #(.width(25)) multiplexer_1 (.in0(Number), .in1(negator_1_out), .out(Result), .sel(Previous_Sign));
endmodule

module SIGN_BIT (
  input  [24:0] Number,
  output Is_Negative
);


  assign Is_Negative = Number[24];
endmodule
